# Fritzing sketch accelgyro (saved by Fritzing 1.0.1rc)
breadboards: 1

parts:
  A1 = photon2
  Part1 = InvenSense MPU6050

nets:
  N1: A1.Pin_2, A1.Pin_31, Part1.VCC
  N2: A1.Pin_4, A1.Pin_30, A1.Pin_35, Part1.GND
  N3: A1.Pin_17, Part1.SDA
  N4: A1.Pin_18, Part1.SCL
  N5: A1.Pin_28, A1.Pin_29

custom parts:
  photon2: The Photon 2 is a development module with a microcontroller and Wi-Fi networking.
